# Fritzing sketch tape_head_pre_amp (saved by Fritzing 0.9.3b)
circuit board: 6.68611cm x 4.67313cm
breadboards: 1

parts:
  NE5532 = LM 358 Dual Op-Amp [package="DIP8 [THT]"]
  1µF_MKT = Ceramic Capacitor [capacitance=1µF voltage=0.1kV package="200 mil [THT, multilayer]"]
  100KΩ = Resistor [tolerance=±5% resistance=100k package=THT]
  68pF = Ceramic Capacitor [capacitance=68pF voltage=0.1kV package="200 mil [THT, multilayer]"]
  100KΩ_2 = Resistor [tolerance=±5% resistance=100k package=THT]
  1KΩ = Resistor [tolerance=±20% resistance=1k package=THT]
  100KΩ_3 = Resistor [tolerance=±5% resistance=100k package=THT]
  100kΩ = Resistor [tolerance=±5% resistance=100k package=THT]
  1_2kΩ = Resistor [tolerance=±5% resistance=1.2k package=THT]
  1_5kΩ = Resistor [tolerance=±5% resistance=1.5k package=THT]
  56kΩ = Resistor [tolerance=±5% resistance=56k package=THT]
  56nF = Ceramic Capacitor [capacitance=56nF voltage=35V package="200 mil [THT, multilayer]"]
  J4 = screw terminal, 2 pins
  J2 = screw terminal, 3 pins
  J3 = screw terminal, 2 pins
  J1 = screw terminal, 3 pins
  220nF = Ceramic Capacitor [capacitance=220nF voltage=16V package="200 mil [THT, multilayer]"]
  220nF_2 = Ceramic Capacitor [capacitance=220nF package="200 mil [THT, multilayer]"]
  470Ω = Resistor [tolerance=±5% resistance=470 package=THT]
  LED = LED - 5mm [color="Red (633nm)" package="5 mm [THT]"]

nets:
  N1: NE5532.connector0, 1µF_MKT.1, 68pF.0, 100KΩ_2.Pin_1
  N2: NE5532.connector1, 68pF.1, 100KΩ_2.Pin_0, 1KΩ.Pin_0
  N3: NE5532.connector2, 100KΩ.Pin_0, 220nF_2.1
  N4: NE5532.connector3, J2.pin1, J1.pin3
  N5: NE5532.connector4, 100kΩ.Pin_1, 220nF.0
  N6: NE5532.connector5, 1_2kΩ.Pin_1, 1_5kΩ.Pin_1
  N7: NE5532.connector6, 56kΩ.Pin_1, 56nF.1, 220nF_2.0
  N8: NE5532.connector7, J2.pin3, J1.pin1, LED.anode
  N9: 1µF_MKT.0, 100KΩ_3.Pin_0, J4.pin1
  GND: 100KΩ.Pin_1, 1KΩ.Pin_1, 100KΩ_3.Pin_1, 100kΩ.Pin_0, 1_2kΩ.Pin_0, J4.pin2, J2.pin2, J3.pin2, J1.pin2, 470Ω.Pin_1
  N10: 1_5kΩ.Pin_0, 56kΩ.Pin_0, 56nF.0
  N11: J3.pin1, 220nF.1
  N12: 470Ω.Pin_0, LED.cathode

notes:
  +12V
  -12V
  GND
  IN
  OUT
  ALL RESISTORS
  METAL FILM
  amplificador
  de cabezal
  de cinta
