# Fritzing sketch tda2003_10W-amp (saved by Fritzing 0.9.3b)
circuit board: 6.97082cm x 5.75541cm
breadboards: 1

parts:
  100µF = Electrolytic Capacitor [capacitance=100nF voltage=35V package="200 mil [THT, electrolytic]"]
  100nF = Ceramic Capacitor [capacitance=100nF package="200 mil [THT, multilayer]"]
  220Ω = Resistor [tolerance=±5% resistance=220 package=THT]
  100nF_2 = Ceramic Capacitor [capacitance=100nF package="200 mil [THT, multilayer]"]
  39nF = Ceramic Capacitor [capacitance=100nF package="200 mil [THT, multilayer]"]
  1Ω = Resistor [tolerance=±5% resistance=220 package=THT]
  2Ω2 = Resistor [tolerance=±5% resistance=220 package=THT]
  1000µF = Electrolytic Capacitor [capacitance=1µF voltage=50V package="200 mil [THT, electrolytic]"]
  470µF = Electrolytic Capacitor [capacitance=1µF voltage=50V package="200 mil [THT, electrolytic]"]
  10µF = Electrolytic Capacitor [capacitance=1µF package="100 mil [THT, electrolytic]"]
  J94 = female pin header, 3 pins [form="♀ (female)"]
  TDA2003 = female pin header, 2 pins [form="♀ (female)"]
  10KΩ = TRIMPOT [package=trim_pot_pth]
  J95 = screw terminal, 2 pins
  J96 = screw terminal, 2 pins
  J98 = screw terminal, 2 pins
  J97 = screw terminal, 2 pins
  39Ω = Resistor [tolerance=±5% resistance=220 package=THT]

nets:
  N1: 100µF.-, 100nF.1, 1Ω.Pin_1, 2Ω2.Pin_0, J94.pin2, 10KΩ.CW, J95.pin2, J96.pin1, J98.pin1, J97.pin2
  N2: 100µF.+, 100nF.0, J94.pin3, J98.pin2, J97.pin1
  N3: 220Ω.Pin_0, 39nF.1, 1000µF.+, TDA2003.pin2
  N4: 220Ω.Pin_1, 2Ω2.Pin_1, 470µF.-
  N5: 100nF_2.0, 1000µF.-, J95.pin1
  N6: 100nF_2.1, 1Ω.Pin_0
  N7: 39nF.0, 39Ω.Pin_0
  N8: 470µF.+, TDA2003.pin1, 39Ω.Pin_1
  N9: 10µF.-, 10KΩ.WIPER
  N10: 10µF.+, J94.pin1
  N11: 10KΩ.CCW, J96.pin2

notes:
  6N138
  7
  SPKR-
  GND
  V+
  IN
  SPKR+
  10W AMP
